# Fritzing sketch DHT11 (saved by Fritzing 0.8.7b)
breadboards: 1

parts:
  DHT11_1 = DHT11 module
  부품1 = Arduino Uno (Rev3)

nets:
  VCC: DHT11_1.VCC, 부품1.5V
  GND: DHT11_1.GND, 부품1.GND
  N1: DHT11_1.DATA, 부품1.D2

custom parts:
  DHT11 module: https://cdn-learn.adafruit.com/downloads/pdf/dht.pdf DHT11 black pcb module reference by:https://github.com/adafruit/Fritzing-Library/blob/master/parts/DHT11%20Humitidy%20and%20Temperature%20Sensor.fzpz
