# Fritzing sketch RC_CAR_CONTROL (saved by Fritzing 0.8.7b)
breadboards: 1

parts:
  부품1 = Arduino Uno (Rev3)
  S1 = H-Bridge with L298N
  J1 = Basic Servo
  M1 = DC Motor

nets:
  N1: 부품1.D9_PWM, J1.pulse
  5V: 부품1.5V, S1.5V, J1.vcc
  GND: 부품1.GND, S1.GND, J1.gnd
  VIN: 부품1.VIN, S1.12V
  N2: S1.M1-01, M1.pin_1
  N3: S1.M1-02, M1.pin_2

custom parts:
  H-Bridge with L298N: h-bridge
