# Fritzing sketch cds_lcd (saved by Fritzing 0.8.7b)
breadboards: 1

parts:
  부품2 = Arduino Uno (Rev3)
  부품1 = LCD1602-I2C
  R1 = Photocell (LDR) [package=THT]
  R2 = Resistor [tolerance=±5% resistance=10k package=THT]

nets:
  N1: 부품2.A0, R1.pin_0, R2.Pin_1
  N2: 부품2.A4/SDA, 부품1.SDA
  N3: 부품2.A5/SCL, 부품1.SCL
  N4: 부품1.GND, R2.Pin_0
  N5: 부품1.VCC, R1.pin_1

custom parts:
  LCD1602-I2C: A standard character display, usually with 2x16 characters. Comes in many colors with LCM1602 IIC attached.
