# Fritzing sketch led2,3,4 (saved by Fritzing 0.8.7b)
breadboards: 1

parts:
  LED1 = LED - 5mm [color="Red (633nm)" package="5 mm [THT]"]
  R1 = Resistor [tolerance=±5% resistance=330 package=THT]
  부품1 = Arduino Uno (Rev3)
  LED2 = LED - 5mm [color="Red (633nm)" package="5 mm [THT]"]
  LED3 = LED - 5mm [color="Red (633nm)" package="5 mm [THT]"]
  R2 = Resistor [tolerance=±5% resistance=330 package=THT]
  R3 = Resistor [tolerance=±5% resistance=330 package=THT]

nets:
  N1: LED1.cathode, R3.Pin_1
  N2: LED1.anode, 부품1.D4
  N3: R1.Pin_0, 부품1.GND, R2.Pin_0, R3.Pin_0
  N4: R1.Pin_1, LED3.cathode
  N5: 부품1.D2, LED2.anode
  N6: 부품1.D3_PWM, LED3.anode
  N7: LED2.cathode, R2.Pin_1
