# Fritzing sketch smart_farm (saved by Fritzing 0.8.7b)
breadboards: 1

parts:
  U1 = Module 4 Relais 5V [package="Module 4 Relais 5V"]
  MH-ET_LIVE_ESP32_DEVKIT1 = MH-ET LIVE ESP32 DEVKIT 38 pins
  PS1 = prefix0000 [part_number=S-350-60]  # not connected
  YF-S201_Flow_Meter2 = YF-S201 Water Flow Meter
  F1 = Fan - Ventilador [package=THT]
  HCMS-29XX1 = HCMS-29xx

nets:
  VCC: U1.VCC, YF-S201_Flow_Meter2.VCC
  GND: U1.GND, MH-ET_LIVE_ESP32_DEVKIT1.GND, YF-S201_Flow_Meter2.GND, F1.GND, HCMS-29XX1.Gnd_LED
  N1: U1.IN1, MH-ET_LIVE_ESP32_DEVKIT1.IO25
  N2: U1.IN2, MH-ET_LIVE_ESP32_DEVKIT1.IO26
  N3: U1.K1-NF, U1.K3-Com, MH-ET_LIVE_ESP32_DEVKIT1.5V
  N4: U1.K2-NO, HCMS-29XX1.V_LED
  N5: U1.K3-NO, F1.5V

notes:
  DC DC converter
  12+
  12-
  5+
  5-
  3+
  3-
  220+
  220-
  220접지
  power adapter
  +
  -

custom parts:
  Module 4 Relais 5V: Module 4 Relais 5V 4x SPD-06VDC-SD-C
  MH-ET LIVE ESP32 DEVKIT 38 pins: http://mh.nodebb.com/topic/2/mh-et-live-esp32-devkit
  YF-S201 Water Flow Meter: The YF-S201 Flow Meter. The input voltage is 5V to 24V (DC).
  Fan - Ventilador: Ventilador de 2 pines, se encuentra comunmente en computadoras de escritorio
